# Fritzing sketch Load Sensors PCB_v2 (saved by Fritzing 0.9.2b)
circuit board: 4.64208cm x 3.06939cm
breadboards: 1

parts:
  J3 = female pin header, 4 pins [form="♀ (female)"]
  J4 = female pin header, 4 pins [form="♀ (female)"]
  J6 = female pin header, 4 pins [form="♀ (female)"]
  J8 = female pin header, 4 pins [form="♀ (female)"]
  J9 = female pin header, 4 pins [form="♀ (female)"]
  J7 = female pin header, 1 pin [form="♀ (female)"]
  J10 = female pin header, 1 pin [form="♀ (female)"]
  J5 = female pin header, 4 pins [form="♀ (female)"]

nets:
  N1: J3.pin1, J4.pin1, J6.pin1, J7.pin1, J5.pin1
  N2: J3.pin2, J8.pin3
  N3: J3.pin3, J8.pin4
  N4: J3.pin4, J4.pin4, J6.pin4, J10.pin1, J5.pin4
  N5: J4.pin2, J9.pin2
  N6: J4.pin3, J9.pin1
  N7: J6.pin2, J9.pin3
  N8: J6.pin3, J9.pin4
  N9: J8.pin1, J5.pin3
  N10: J8.pin2, J5.pin2
